// Logisim project 8.bitCPU.circ as structural Verilog: 14 circuits, main circuit equalcomparator
module equalcomparator (
  input  [7:0] X,
  input  [7:0] Y,
  output eq
);

  wire and_1_out, and_2_out, and_3_out, and_4_out, and_5_out, and_6_out, not_1_out, not_2_out, not_3_out,
       not_4_out, not_5_out, not_6_out, not_7_out, not_8_out, xor_1_out, xor_2_out, xor_3_out, xor_4_out,
       xor_5_out, xor_6_out, xor_7_out, xor_8_out;

  xor xor_1 (xor_1_out, X[0], Y[0]);
  not not_1 (not_1_out, xor_1_out);
  xor xor_2 (xor_2_out, X[1], Y[1]);
  not not_2 (not_2_out, xor_2_out);
  xor xor_3 (xor_3_out, X[2], Y[2]);
  not not_3 (not_3_out, xor_3_out);
  xor xor_4 (xor_4_out, X[3], Y[3]);
  not not_4 (not_4_out, xor_4_out);
  xor xor_5 (xor_5_out, X[4], Y[4]);
  not not_5 (not_5_out, xor_5_out);
  xor xor_6 (xor_6_out, X[5], Y[5]);
  not not_6 (not_6_out, xor_6_out);
  xor xor_7 (xor_7_out, X[6], Y[6]);
  not not_7 (not_7_out, xor_7_out);
  xor xor_8 (xor_8_out, X[7], Y[7]);
  not not_8 (not_8_out, xor_8_out);
  and and_1 (and_1_out, not_1_out, not_2_out);
  and and_2 (and_2_out, not_3_out, not_4_out);
  and and_3 (and_3_out, not_5_out, not_6_out);
  and and_4 (and_4_out, not_7_out, not_8_out);
  and and_5 (and_5_out, and_1_out, and_2_out);
  and and_6 (and_6_out, and_3_out, and_4_out);
  and and_7 (eq, and_5_out, and_6_out);
endmodule

module lessthancomparator (
  input  [7:0] X,
  input  [7:0] Y,
  output less
);

  wire and_1_out, and_2_out, and_3_out, and_4_out, and_5_out, and_6_out, and_7_out, and_8_out, and_9_out,
       and_10_out, and_11_out, and_12_out, and_13_out, e0_out, e1_out, e2_out, e3_out, e4_out, e5_out,
       e6_out, e7_out, l0_out, l1_out, l2_out, l3_out, l4_out, l5_out, l6_out, l7_out, not_1_out, not_2_out,
       not_3_out, not_4_out, not_5_out, not_6_out, not_7_out, not_8_out, not_10_out, not_11_out, not_12_out,
       not_13_out, not_14_out, not_15_out, not_16_out, or_1_out, or_2_out, or_3_out, or_4_out, or_5_out,
       or_6_out;

  not not_1 (not_1_out, X[0]);
  not not_2 (not_2_out, X[1]);
  not not_3 (not_3_out, X[2]);
  not not_4 (not_4_out, X[3]);
  not not_5 (not_5_out, X[4]);
  not not_6 (not_6_out, X[5]);
  not not_7 (not_7_out, X[6]);
  not not_8 (not_8_out, X[7]);
  xor e0 (e0_out, X[0], Y[0]);
  xor e1 (e1_out, X[1], Y[1]);
  xor e2 (e2_out, X[2], Y[2]);
  xor e3 (e3_out, X[3], Y[3]);
  xor e4 (e4_out, X[4], Y[4]);
  xor e5 (e5_out, X[5], Y[5]);
  xor e6 (e6_out, X[6], Y[6]);
  xor e7 (e7_out, X[7], Y[7]);
  and l0 (l0_out, not_1_out, Y[0]);
  and l1 (l1_out, not_2_out, Y[1]);
  and l2 (l2_out, not_3_out, Y[2]);
  and l3 (l3_out, not_4_out, Y[3]);
  and l4 (l4_out, not_5_out, Y[4]);
  and l5 (l5_out, not_6_out, Y[5]);
  and l6 (l6_out, not_7_out, Y[6]);
  and l7 (l7_out, not_8_out, Y[7]);
  // NOT_Gate not_9 has open pins: in=e0_out, out=open
  not not_10 (not_10_out, e1_out);
  not not_11 (not_11_out, e2_out);
  not not_12 (not_12_out, e3_out);
  not not_13 (not_13_out, e4_out);
  not not_14 (not_14_out, e5_out);
  not not_15 (not_15_out, e6_out);
  not not_16 (not_16_out, e7_out);
  and and_1 (and_1_out, l6_out, not_16_out);
  and and_2 (and_2_out, not_15_out, not_16_out);
  and and_3 (and_3_out, not_14_out, and_2_out);
  and and_4 (and_4_out, l5_out, and_2_out);
  and and_5 (and_5_out, not_13_out, and_3_out);
  and and_6 (and_6_out, l4_out, and_3_out);
  and and_7 (and_7_out, not_12_out, and_5_out);
  and and_8 (and_8_out, l3_out, and_5_out);
  or or_1 (or_1_out, and_6_out, and_4_out);
  and and_9 (and_9_out, not_11_out, and_7_out);
  and and_10 (and_10_out, l2_out, and_7_out);
  and and_11 (and_11_out, not_10_out, and_9_out);
  and and_12 (and_12_out, l1_out, and_9_out);
  or or_2 (or_2_out, and_8_out, or_1_out);
  and and_13 (and_13_out, l0_out, and_11_out);
  or or_3 (or_3_out, and_10_out, or_2_out);
  or or_4 (or_4_out, and_12_out, or_3_out);
  or or_5 (or_5_out, and_13_out, or_4_out);
  or or_6 (or_6_out, l7_out, or_5_out);
  or or_7 (less, and_1_out, or_6_out);
endmodule

module fullAdder8 (
  input  CIN,
  input  [7:0] X,
  input  [7:0] Y,
  output [7:0] SUM,
  output COUT
);

  wire and_1_out, and_2_out, and_3_out, and_4_out, and_5_out, and_6_out, and_7_out, and_8_out, and_9_out,
       and_10_out, and_11_out, and_12_out, and_13_out, and_14_out, and_15_out, and_16_out, or_1_out,
       or_2_out, or_3_out, or_4_out, or_5_out, or_6_out, or_7_out, xor_1_out, xor_2_out, xor_3_out,
       xor_4_out, xor_5_out, xor_6_out, xor_7_out, xor_8_out;

  xor xor_1 (xor_1_out, X[0], Y[0]);
  and and_1 (and_1_out, X[0], Y[0]);
  xor xor_2 (xor_2_out, X[1], Y[1]);
  and and_2 (and_2_out, X[1], Y[1]);
  xor xor_3 (xor_3_out, X[2], Y[2]);
  and and_3 (and_3_out, X[2], Y[2]);
  xor xor_4 (xor_4_out, X[3], Y[3]);
  and and_4 (and_4_out, X[3], Y[3]);
  xor xor_5 (xor_5_out, X[4], Y[4]);
  and and_5 (and_5_out, X[4], Y[4]);
  xor xor_6 (xor_6_out, X[5], Y[5]);
  and and_6 (and_6_out, X[5], Y[5]);
  xor xor_7 (xor_7_out, X[6], Y[6]);
  and and_7 (and_7_out, X[6], Y[6]);
  xor xor_8 (xor_8_out, X[7], Y[7]);
  and and_8 (and_8_out, X[7], Y[7]);
  and and_9 (and_9_out, CIN, xor_1_out);
  and and_10 (and_10_out, or_1_out, xor_2_out);
  and and_11 (and_11_out, or_2_out, xor_3_out);
  and and_12 (and_12_out, or_3_out, xor_4_out);
  and and_13 (and_13_out, or_4_out, xor_5_out);
  and and_14 (and_14_out, or_5_out, xor_6_out);
  and and_15 (and_15_out, or_6_out, xor_7_out);
  and and_16 (and_16_out, or_7_out, xor_8_out);
  xor xor_9 (SUM[0], CIN, xor_1_out);
  or or_1 (or_1_out, and_9_out, and_1_out);
  xor xor_10 (SUM[1], or_1_out, xor_2_out);
  or or_2 (or_2_out, and_10_out, and_2_out);
  xor xor_11 (SUM[2], or_2_out, xor_3_out);
  or or_3 (or_3_out, and_11_out, and_3_out);
  xor xor_12 (SUM[3], or_3_out, xor_4_out);
  or or_4 (or_4_out, and_12_out, and_4_out);
  xor xor_13 (SUM[4], or_4_out, xor_5_out);
  or or_5 (or_5_out, and_13_out, and_5_out);
  xor xor_14 (SUM[5], or_5_out, xor_6_out);
  or or_6 (or_6_out, and_14_out, and_6_out);
  xor xor_15 (SUM[6], or_6_out, xor_7_out);
  or or_7 (or_7_out, and_15_out, and_7_out);
  xor xor_16 (SUM[7], or_7_out, xor_8_out);
  or or_8 (COUT, and_16_out, and_8_out);
endmodule

module twosComplement (
  input  [7:0] X,
  output [7:0] twos_complement
);

  wire [7:0] not_1_out;

  not not_1 (not_1_out[0], X[0]);
  not not_2 (not_1_out[1], X[1]);
  not not_3 (not_1_out[2], X[2]);
  not not_4 (not_1_out[3], X[3]);
  not not_5 (not_1_out[4], X[4]);
  not not_6 (not_1_out[5], X[5]);
  not not_7 (not_1_out[6], X[6]);
  not not_8 (not_1_out[7], X[7]);
  fullAdder8 fulladder8_1 (.X(not_1_out), .Y(8'h1), .SUM(twos_complement));  // open: CIN, COUT
endmodule

module multipler (
  input  [7:0] X,
  input  [7:0] Y,
  output [7:0] MULT
);

  wire [7:0] fulladder8_1_sum, fulladder8_2_sum, fulladder8_3_sum, fulladder8_4_sum, fulladder8_5_sum,
       fulladder8_6_sum, leftshifter_1_left, leftshifter_2_left, leftshifter_3_left, leftshifter_4_left,
       leftshifter_5_left, leftshifter_6_left, leftshifter_7_left, leftshifter_8_left,
       partialproduct_1_output1, partialproduct_1_output2, partialproduct_1_output3,
       partialproduct_1_output4, partialproduct_1_output5, partialproduct_1_output6,
       partialproduct_1_output7, partialproduct_1_output8;

  partialproduct partialproduct_1 (
    .inputA(X), .inputB(Y), .output1(partialproduct_1_output1), .output3(partialproduct_1_output3),
    .output5(partialproduct_1_output5), .output6(partialproduct_1_output6),
    .output2(partialproduct_1_output2), .output4(partialproduct_1_output4),
    .output7(partialproduct_1_output7), .output8(partialproduct_1_output8));
  leftshifter leftshifter_1 (.X(partialproduct_1_output1), .AMNT(3'b000), .left(leftshifter_1_left));
  leftshifter leftshifter_2 (.X(partialproduct_1_output2), .AMNT(3'b001), .left(leftshifter_2_left));
  leftshifter leftshifter_3 (.X(partialproduct_1_output3), .AMNT(3'b010), .left(leftshifter_3_left));
  leftshifter leftshifter_4 (.X(partialproduct_1_output4), .AMNT(3'b011), .left(leftshifter_4_left));
  leftshifter leftshifter_5 (.X(partialproduct_1_output5), .AMNT(3'b100), .left(leftshifter_5_left));
  leftshifter leftshifter_6 (.X(partialproduct_1_output6), .AMNT(3'b101), .left(leftshifter_6_left));
  leftshifter leftshifter_7 (.X(partialproduct_1_output7), .AMNT(3'b110), .left(leftshifter_7_left));
  leftshifter leftshifter_8 (.X(partialproduct_1_output8), .AMNT(3'b111), .left(leftshifter_8_left));
  fullAdder8 fulladder8_1 (
    .CIN(1'b0), .X(leftshifter_1_left), .Y(leftshifter_2_left), .SUM(fulladder8_1_sum));  // open: COUT
  fullAdder8 fulladder8_2 (
    .CIN(1'b0), .X(fulladder8_1_sum), .Y(leftshifter_3_left), .SUM(fulladder8_2_sum));  // open: COUT
  fullAdder8 fulladder8_3 (
    .CIN(1'b0), .X(fulladder8_2_sum), .Y(leftshifter_4_left), .SUM(fulladder8_3_sum));  // open: COUT
  fullAdder8 fulladder8_4 (
    .CIN(1'b0), .X(fulladder8_3_sum), .Y(leftshifter_5_left), .SUM(fulladder8_4_sum));  // open: COUT
  fullAdder8 fulladder8_5 (
    .CIN(1'b0), .X(fulladder8_4_sum), .Y(leftshifter_6_left), .SUM(fulladder8_5_sum));  // open: COUT
  fullAdder8 fulladder8_6 (
    .CIN(1'b0), .X(fulladder8_5_sum), .Y(leftshifter_7_left), .SUM(fulladder8_6_sum));  // open: COUT
  fullAdder8 fulladder8_7 (.CIN(1'b0), .X(fulladder8_6_sum), .Y(leftshifter_8_left), .SUM(MULT));  // open: COUT
endmodule

module leftshifter (
  input  [7:0] X,
  input  [2:0] AMNT,
  output [7:0] left
);

  wire multiplexer_1_out, multiplexer_2_out, multiplexer_3_out, multiplexer_4_out, multiplexer_5_out,
       multiplexer_6_out, multiplexer_7_out, multiplexer_8_out, multiplexer_9_out, multiplexer_10_out,
       multiplexer_11_out, multiplexer_12_out, multiplexer_13_out, multiplexer_14_out, multiplexer_15_out,
       multiplexer_16_out;

  Multiplexer multiplexer_1 (.in0(X[0]), .in1(1'b0), .out(multiplexer_1_out), .sel(AMNT[0]));
  Multiplexer multiplexer_2 (.in0(X[1]), .in1(X[0]), .out(multiplexer_2_out), .sel(AMNT[0]));
  Multiplexer multiplexer_3 (.in0(X[2]), .in1(X[1]), .out(multiplexer_3_out), .sel(AMNT[0]));
  Multiplexer multiplexer_4 (.in0(X[3]), .in1(X[2]), .out(multiplexer_4_out), .sel(AMNT[0]));
  Multiplexer multiplexer_5 (.in0(X[4]), .in1(X[3]), .out(multiplexer_5_out), .sel(AMNT[0]));
  Multiplexer multiplexer_6 (.in0(X[5]), .in1(X[4]), .out(multiplexer_6_out), .sel(AMNT[0]));
  Multiplexer multiplexer_7 (.in0(X[6]), .in1(X[5]), .out(multiplexer_7_out), .sel(AMNT[0]));
  Multiplexer multiplexer_8 (.in0(X[7]), .in1(X[6]), .out(multiplexer_8_out), .sel(AMNT[0]));
  Multiplexer multiplexer_9 (.in0(multiplexer_1_out), .in1(1'b0), .out(multiplexer_9_out), .sel(AMNT[1]));
  Multiplexer multiplexer_10 (.in0(multiplexer_2_out), .in1(1'b0), .out(multiplexer_10_out), .sel(AMNT[1]));
  Multiplexer multiplexer_11 (
    .in0(multiplexer_3_out), .in1(multiplexer_1_out), .out(multiplexer_11_out), .sel(AMNT[1]));
  Multiplexer multiplexer_12 (
    .in0(multiplexer_4_out), .in1(multiplexer_2_out), .out(multiplexer_12_out), .sel(AMNT[1]));
  Multiplexer multiplexer_13 (
    .in0(multiplexer_5_out), .in1(multiplexer_3_out), .out(multiplexer_13_out), .sel(AMNT[1]));
  Multiplexer multiplexer_14 (
    .in0(multiplexer_6_out), .in1(multiplexer_4_out), .out(multiplexer_14_out), .sel(AMNT[1]));
  Multiplexer multiplexer_15 (
    .in0(multiplexer_7_out), .in1(multiplexer_5_out), .out(multiplexer_15_out), .sel(AMNT[1]));
  Multiplexer multiplexer_16 (
    .in0(multiplexer_8_out), .in1(multiplexer_6_out), .out(multiplexer_16_out), .sel(AMNT[1]));
  Multiplexer multiplexer_17 (.in0(multiplexer_9_out), .in1(1'b0), .out(left[0]), .sel(AMNT[2]));
  Multiplexer multiplexer_18 (.in0(multiplexer_10_out), .in1(1'b0), .out(left[1]), .sel(AMNT[2]));
  Multiplexer multiplexer_19 (.in0(multiplexer_11_out), .in1(1'b0), .out(left[2]), .sel(AMNT[2]));
  Multiplexer multiplexer_20 (.in0(multiplexer_12_out), .in1(1'b0), .out(left[3]), .sel(AMNT[2]));
  Multiplexer multiplexer_21 (.in0(multiplexer_13_out), .in1(multiplexer_9_out), .out(left[4]), .sel(AMNT[2]));
  Multiplexer multiplexer_22 (.in0(multiplexer_14_out), .in1(multiplexer_10_out), .out(left[5]), .sel(AMNT[2]));
  Multiplexer multiplexer_23 (.in0(multiplexer_15_out), .in1(multiplexer_11_out), .out(left[6]), .sel(AMNT[2]));
  Multiplexer multiplexer_24 (.in0(multiplexer_16_out), .in1(multiplexer_12_out), .out(left[7]), .sel(AMNT[2]));
endmodule

module rightshifter (
  input  [7:0] in_1,
  input  [2:0] in_2,
  output [7:0] out_3
);

  wire multiplexer_1_out, multiplexer_2_out, multiplexer_3_out, multiplexer_4_out, multiplexer_5_out,
       multiplexer_6_out, multiplexer_7_out, multiplexer_8_out, multiplexer_9_out, multiplexer_10_out,
       multiplexer_11_out, multiplexer_12_out, multiplexer_13_out, multiplexer_14_out, multiplexer_15_out,
       multiplexer_16_out;

  Multiplexer multiplexer_1 (.in0(in_1[0]), .in1(in_1[1]), .out(multiplexer_1_out), .sel(in_2[0]));
  Multiplexer multiplexer_2 (.in0(in_1[1]), .in1(in_1[2]), .out(multiplexer_2_out), .sel(in_2[0]));
  Multiplexer multiplexer_3 (.in0(in_1[2]), .in1(in_1[3]), .out(multiplexer_3_out), .sel(in_2[0]));
  Multiplexer multiplexer_4 (.in0(in_1[3]), .in1(in_1[4]), .out(multiplexer_4_out), .sel(in_2[0]));
  Multiplexer multiplexer_5 (.in0(in_1[4]), .in1(in_1[5]), .out(multiplexer_5_out), .sel(in_2[0]));
  Multiplexer multiplexer_6 (.in0(in_1[5]), .in1(in_1[6]), .out(multiplexer_6_out), .sel(in_2[0]));
  Multiplexer multiplexer_7 (.in0(in_1[6]), .in1(in_1[7]), .out(multiplexer_7_out), .sel(in_2[0]));
  Multiplexer multiplexer_8 (.in0(in_1[7]), .in1(1'b0), .out(multiplexer_8_out), .sel(in_2[0]));
  Multiplexer multiplexer_9 (.in0(multiplexer_1_out), .in1(multiplexer_3_out), .out(multiplexer_9_out), .sel(in_2[1]));
  Multiplexer multiplexer_10 (
    .in0(multiplexer_2_out), .in1(multiplexer_4_out), .out(multiplexer_10_out), .sel(in_2[1]));
  Multiplexer multiplexer_11 (
    .in0(multiplexer_3_out), .in1(multiplexer_5_out), .out(multiplexer_11_out), .sel(in_2[1]));
  Multiplexer multiplexer_12 (
    .in0(multiplexer_4_out), .in1(multiplexer_6_out), .out(multiplexer_12_out), .sel(in_2[1]));
  Multiplexer multiplexer_13 (
    .in0(multiplexer_5_out), .in1(multiplexer_7_out), .out(multiplexer_13_out), .sel(in_2[1]));
  Multiplexer multiplexer_14 (
    .in0(multiplexer_6_out), .in1(multiplexer_8_out), .out(multiplexer_14_out), .sel(in_2[1]));
  Multiplexer multiplexer_15 (.in0(multiplexer_7_out), .in1(1'b0), .out(multiplexer_15_out), .sel(in_2[1]));
  Multiplexer multiplexer_16 (.in0(multiplexer_8_out), .in1(1'b0), .out(multiplexer_16_out), .sel(in_2[1]));
  Multiplexer multiplexer_17 (.in0(multiplexer_9_out), .in1(multiplexer_13_out), .out(out_3[0]), .sel(in_2[2]));
  Multiplexer multiplexer_18 (.in0(multiplexer_10_out), .in1(multiplexer_14_out), .out(out_3[1]), .sel(in_2[2]));
  Multiplexer multiplexer_19 (.in0(multiplexer_11_out), .in1(multiplexer_15_out), .out(out_3[2]), .sel(in_2[2]));
  Multiplexer multiplexer_20 (.in0(multiplexer_12_out), .in1(multiplexer_16_out), .out(out_3[3]), .sel(in_2[2]));
  Multiplexer multiplexer_21 (.in0(multiplexer_13_out), .in1(1'b0), .out(out_3[4]), .sel(in_2[2]));
  Multiplexer multiplexer_22 (.in0(multiplexer_14_out), .in1(1'b0), .out(out_3[5]), .sel(in_2[2]));
  Multiplexer multiplexer_23 (.in0(multiplexer_15_out), .in1(1'b0), .out(out_3[6]), .sel(in_2[2]));
  Multiplexer multiplexer_24 (.in0(multiplexer_16_out), .in1(1'b0), .out(out_3[7]), .sel(in_2[2]));
endmodule

module partialproduct (
  input  [7:0] inputA,
  input  [7:0] inputB,
  output [7:0] output1,
  output [7:0] output3,
  output [7:0] output5,
  output [7:0] output6,
  output [7:0] output2,
  output [7:0] output4,
  output [7:0] output7,
  output [7:0] output8
);

  and and_1 (output1[0], inputB[0], inputA[0]);
  and and_2 (output1[1], inputB[0], inputA[1]);
  and and_3 (output1[2], inputB[0], inputA[2]);
  and and_4 (output1[3], inputB[0], inputA[3]);
  and and_5 (output1[4], inputB[0], inputA[4]);
  and and_6 (output1[5], inputB[0], inputA[5]);
  and and_7 (output1[6], inputB[0], inputA[6]);
  and and_8 (output1[7], inputB[0], inputA[7]);
  and and_9 (output2[0], inputB[1], inputA[0]);
  and and_10 (output2[1], inputB[1], inputA[1]);
  and and_11 (output2[2], inputB[1], inputA[2]);
  and and_12 (output2[3], inputB[1], inputA[3]);
  and and_13 (output2[4], inputB[1], inputA[4]);
  and and_14 (output2[5], inputB[1], inputA[5]);
  and and_15 (output2[6], inputB[1], inputA[6]);
  and and_16 (output2[7], inputB[1], inputA[7]);
  and and_17 (output3[0], inputB[2], inputA[0]);
  and and_18 (output3[1], inputB[2], inputA[1]);
  and and_19 (output3[2], inputB[2], inputA[2]);
  and and_20 (output3[3], inputB[2], inputA[3]);
  and and_21 (output3[4], inputB[2], inputA[4]);
  and and_22 (output3[5], inputB[2], inputA[5]);
  and and_23 (output3[6], inputB[2], inputA[6]);
  and and_24 (output3[7], inputB[2], inputA[7]);
  and and_25 (output4[0], inputB[3], inputA[0]);
  and and_26 (output4[1], inputB[3], inputA[1]);
  and and_27 (output4[2], inputB[3], inputA[2]);
  and and_28 (output4[3], inputB[3], inputA[3]);
  and and_29 (output4[4], inputB[3], inputA[4]);
  and and_30 (output4[5], inputB[3], inputA[5]);
  and and_31 (output4[6], inputB[3], inputA[6]);
  and and_32 (output4[7], inputB[3], inputA[7]);
  and and_33 (output5[0], inputB[4], inputA[0]);
  and and_34 (output5[1], inputB[4], inputA[1]);
  and and_35 (output5[2], inputB[4], inputA[2]);
  and and_36 (output5[3], inputB[4], inputA[3]);
  and and_37 (output5[4], inputB[4], inputA[4]);
  and and_38 (output5[5], inputB[4], inputA[5]);
  and and_39 (output5[6], inputB[4], inputA[6]);
  and and_40 (output5[7], inputB[4], inputA[7]);
  and and_41 (output7[0], inputB[5], inputA[0]);
  and and_42 (output7[1], inputB[5], inputA[1]);
  and and_43 (output7[2], inputB[5], inputA[2]);
  and and_44 (output7[3], inputB[5], inputA[3]);
  and and_45 (output7[4], inputB[5], inputA[4]);
  and and_46 (output7[5], inputB[5], inputA[5]);
  and and_47 (output7[6], inputB[5], inputA[6]);
  and and_48 (output7[7], inputB[5], inputA[7]);
  and and_49 (output6[0], inputB[6], inputA[0]);
  and and_50 (output6[1], inputB[6], inputA[1]);
  and and_51 (output6[2], inputB[6], inputA[2]);
  and and_52 (output6[3], inputB[6], inputA[3]);
  and and_53 (output6[4], inputB[6], inputA[4]);
  and and_54 (output6[5], inputB[6], inputA[5]);
  and and_55 (output6[6], inputB[6], inputA[6]);
  and and_56 (output6[7], inputB[6], inputA[7]);
  and and_57 (output8[0], inputB[7], inputA[0]);
  and and_58 (output8[1], inputB[7], inputA[1]);
  and and_59 (output8[2], inputB[7], inputA[2]);
  and and_60 (output8[3], inputB[7], inputA[3]);
  and and_61 (output8[4], inputB[7], inputA[4]);
  and and_62 (output8[5], inputB[7], inputA[5]);
  and and_63 (output8[6], inputB[7], inputA[6]);
  and and_64 (output8[7], inputB[7], inputA[7]);
endmodule

module alu8 (
  input  [7:0] X,
  input  [1:0] opcode,
  input  [7:0] Y,
  output [7:0] m_out
);

  wire [7:0] fulladder8_1_sum, multipler_1_mult, or_1_out;

  assign or_1_out = X | Y;  // OR_Gate or_1, 8 bits wide
  fullAdder8 fulladder8_1 (.X(X), .Y(Y), .SUM(fulladder8_1_sum));  // open: CIN, COUT
  multipler multipler_1 (.X(X), .Y(Y), .MULT(multipler_1_mult));
  Multiplexer #(.select(2), .width(8)) multiplexer_1 (
    .in0(fulladder8_1_sum), .in1(fulladder8_1_sum), .in2(or_1_out), .in3(multipler_1_mult), .out(m_out),
    .sel(opcode));
endmodule

module Register_file (
  input  WE,
  input  [2:0] M3,
  input  [7:0] Data_In,
  input  CLK,
  input  [2:0] RS,
  input  [2:0] RT,
  output [7:0] RS_Out,
  output [7:0] RT_Out
);

  wire decoder_1_out0, decoder_1_out1, decoder_1_out2, decoder_1_out3, decoder_1_out4, decoder_1_out5,
       decoder_1_out6, decoder_1_out7;
  wire [7:0] register_1_q, register_2_q, register_3_q, register_4_q, register_5_q, register_6_q,
       register_7_q, register_8_q;

  Multiplexer #(.select(3), .width(8)) multiplexer_1 (
    .in0(register_1_q), .in1(register_2_q), .in2(register_3_q), .in3(register_4_q), .in4(register_5_q),
    .in5(register_6_q), .in6(register_7_q), .in7(register_8_q), .out(RS_Out), .sel(RS));
  Multiplexer #(.select(3), .width(8)) multiplexer_2 (
    .in0(register_1_q), .in1(register_2_q), .in2(register_3_q), .in3(register_4_q), .in4(register_5_q),
    .in5(register_6_q), .in6(register_7_q), .in7(register_8_q), .out(RT_Out), .sel(RT));
  Decoder #(.select(3)) decoder_1 (
    .out0(decoder_1_out0), .out1(decoder_1_out1), .out2(decoder_1_out2), .out3(decoder_1_out3),
    .out4(decoder_1_out4), .out5(decoder_1_out5), .out6(decoder_1_out6), .out7(decoder_1_out7), .sel(M3),
    .en(WE));
  Register register_1 (.D(Data_In), .en(decoder_1_out0), .clk(CLK), .Q(register_1_q));  // open: clr
  Register register_2 (.D(Data_In), .en(decoder_1_out1), .clk(CLK), .Q(register_2_q));  // open: clr
  Register register_3 (.D(Data_In), .en(decoder_1_out2), .clk(CLK), .Q(register_3_q));  // open: clr
  Register register_4 (.D(Data_In), .en(decoder_1_out3), .clk(CLK), .Q(register_4_q));  // open: clr
  Register register_5 (.D(Data_In), .en(decoder_1_out4), .clk(CLK), .Q(register_5_q));  // open: clr
  Register register_6 (.D(Data_In), .en(decoder_1_out5), .clk(CLK), .Q(register_6_q));  // open: clr
  Register register_7 (.D(Data_In), .en(decoder_1_out6), .clk(CLK), .Q(register_7_q));  // open: clr
  Register register_8 (.D(Data_In), .en(decoder_1_out7), .clk(CLK), .Q(register_8_q));  // open: clr
endmodule

module CPU_8bit (
);

  wire CLK_out, control_unit_1_m2, control_unit_1_m3, control_unit_1_read, control_unit_1_we,
       control_unit_1_write;
  wire [1:0] control_unit_1_alu_funct, control_unit_1_m1;
  wire [2:0] multiplexer_1_out;
  wire [3:0] rom_1_data_2;
  wire [7:0] alu8_1_m_out, fulladder8_1_sum, multiplexer_2_out, multiplexer_3_out, ram_1_dout, register_1_q,
       register_file_1_rs_out, register_file_1_rt_out;
  wire [19:0] rom_1_data;

  Clock CLK (.out(CLK_out));
  Register register_1 (.D(fulladder8_1_sum), .clk(CLK_out), .Q(register_1_q));  // open: en, clr
  fullAdder8 fulladder8_1 (.X(register_1_q), .Y(8'h1), .SUM(fulladder8_1_sum));  // open: CIN, COUT
  ROM #(.dataWidth(24)) rom_1 (.addr(register_1_q), .data({rom_1_data_2, rom_1_data}));
  Control_Unit control_unit_1 (
    .Opcode(rom_1_data_2), .M1(control_unit_1_m1), .WE(control_unit_1_we), .Write(control_unit_1_write),
    .Read(control_unit_1_read), .M3(control_unit_1_m3), .Alu_funct(control_unit_1_alu_funct),
    .M2(control_unit_1_m2));
  Multiplexer #(.width(3)) multiplexer_1 (
    .in0(3'b111), .in1(rom_1_data[13:11]), .out(multiplexer_1_out), .sel(control_unit_1_m3));
  Multiplexer #(.select(2), .width(8)) multiplexer_2 (
    .in0(alu8_1_m_out), .in1(ram_1_dout), .in2(rom_1_data[7:0]), .out(multiplexer_2_out),
    .sel(control_unit_1_m1));  // open: in3
  Register_file register_file_1 (
    .WE(control_unit_1_we), .M3(multiplexer_1_out), .Data_In(multiplexer_2_out), .CLK(CLK_out),
    .RS(rom_1_data[19:17]), .RT(rom_1_data[16:14]), .RS_Out(register_file_1_rs_out),
    .RT_Out(register_file_1_rt_out));
  Multiplexer #(.width(8)) multiplexer_3 (
    .in0(register_file_1_rt_out), .in1(rom_1_data[7:0]), .out(multiplexer_3_out), .sel(control_unit_1_m2));
  alu8 alu8_1 (
    .X(register_file_1_rs_out), .opcode(control_unit_1_alu_funct), .Y(multiplexer_3_out), .m_out(alu8_1_m_out));
  RAM ram_1 (
    .addr(register_file_1_rt_out), .we(control_unit_1_write), .oe(control_unit_1_read), .clk(CLK_out),
    .din(alu8_1_m_out), .dout(ram_1_dout));

  // Notes on the sheet:
  //   contents of rom_1 (hex, n*v repeats v):
  //   300a2 30083 ca800 27001 10181 4c800 88803 7300 20303 212312
endmodule

module instruction_memory (
  input  [7:0] PC_input,
  output [3:0] OpCode,
  output [2:0] RS,
  output [2:0] RT,
  output [2:0] RD,
  output [7:0] Immediate
);

  wire [10:8] rom_1_data;

  ROM #(.dataWidth(24)) rom_1 (.addr(PC_input), .data({OpCode, RS, RT, RD, rom_1_data, Immediate}));

  // Notes on the sheet:
  //   contents of rom_1 (hex, n*v repeats v):
  //   212312
endmodule

module Data_Memory (
  input  [7:0] RT,
  input  Write,
  input  Read,
  input  CLK,
  input  [7:0] Alu,
  output [7:0] M1_Out
);

  RAM ram_1 (.addr(RT), .we(Write), .oe(Read), .clk(CLK), .din(Alu), .dout(M1_Out));
endmodule

module Control_Unit (
  input  [3:0] Opcode,
  output [1:0] M1,
  output WE,
  output Write,
  output Read,
  output M3,
  output [1:0] Alu_funct,
  output M2
);

  wire not_1_out, not_2_out, not_4_out, xor_1_out;

  not not_1 (not_1_out, Opcode[0]);
  nand nand_1 (Read, Opcode[1], Opcode[0]);
  and and_1 (M3, Opcode[2], Opcode[3]);
  and and_2 (M1[1], Opcode[0], Opcode[1]);
  and and_3 (Write, Opcode[1], not_1_out);
  not not_2 (not_2_out, Opcode[2]);
  ExactlyOne xor_1 (.out(xor_1_out), .in0(Opcode[0]), .in1(Opcode[1]), .in2(Opcode[2]), .in3(Opcode[3]));
  not not_3 (M1[0], M1[1]);
  not not_4 (not_4_out, Opcode[1]);
  and and_4 (M2, not_2_out, xor_1_out);
  or or_1 (WE, not_4_out, Opcode[0]);

  assign Alu_funct = Opcode[3:2];
endmodule
